// Logisim project oblArqui.circ as structural Verilog: 12 circuits, main circuit main
module main (
);

  wire and_1_out, and_2_out, button_1_out, button_2_out, button_3_out, button_4_out, button_5_out,
       button_6_out, button_7_out, button_8_out, button_9_out, comparator_1_eq, comparator_1_gt,
       comparator_2_eq, comparator_2_gt, comparator_3_eq, comparator_3_gt, comparator_4_eq, comparator_4_gt,
       comparator_5_eq, comparator_5_gt, contadorbin_1_led1, contadorbin_1_led2, contadorbin_1_led3,
       contadorbin_1_led4, contadorbin_1_led5, contadorbin_1_led6, contadorbin_1_led7, contadorbin_1_led8,
       contadorbin_1_led9, contadorbin_1_led10, nivelvelocidad_1_velocidad1, nivelvelocidad_1_velocidad2,
       nivelvelocidad_1_velocidad3, or_1_out, or_2_out, or_3_out, or_4_out, or_5_out, or_6_out, or_7_out,
       or_8_out, puntajerecord_1_led1, puntajerecord_1_led2, puntajerecord_1_led3, puntajerecord_1_led4,
       puntajerecord_1_led5, puntajerecord_1_led6, puntajerecord_1_led7, puntajerecord_1_led8,
       puntajerecord_1_led9, puntajerecord_1_led10, reductorfrecuencia2_1_relojdividido,
       reductorfrecuencia4_1_relojdividido, Reloj;
  wire [2:0] bit_extender_1_out, bit_extender_2_out, bit_extender_3_out, bit_extender_4_out,
       bit_extender_5_out, movimientocuadrado_1_colactual;
  wire [3:0] contador2_1_puntos1, contador2_1_puntos2, contador2_1_puntos3, contador2_1_puntos4,
       puntajerecordhexa_1_record1, puntajerecordhexa_1_record2, puntajerecordhexa_1_record3,
       puntajerecordhexa_1_record4;
  wire [4:0] movimientocuadrado_1_inicio;
  wire [7:0] guardarnuevoestado_1_col_0, guardarnuevoestado_1_col_1, guardarnuevoestado_1_col_2,
       guardarnuevoestado_1_col_3, guardarnuevoestado_1_col_4, movimientocuadrado_1_col0,
       movimientocuadrado_1_col1, movimientocuadrado_1_col2, movimientocuadrado_1_col3,
       movimientocuadrado_1_col4, movimientocuadrado_1_filaactual, shifter_1_out, shifter_2_out,
       shifter_3_out, shifter_4_out, shifter_5_out, xor_1_out, xor_2_out, xor_3_out, xor_4_out, xor_5_out;

  NivelVelocidad nivelvelocidad_1 (
    .Entrada(button_6_out), .Reset(button_8_out), .velocidad1(nivelvelocidad_1_velocidad1),
    .velocidad2(nivelvelocidad_1_velocidad2), .velocidad3(nivelvelocidad_1_velocidad3));
  or or_1 (or_1_out, nivelvelocidad_1_velocidad2, button_8_out);
  or or_2 (or_2_out, nivelvelocidad_1_velocidad3, button_8_out);
  and and_1 (and_1_out, Reloj, nivelvelocidad_1_velocidad3);
  Clock clock_1 (.out(Reloj));
  ReductorFrecuencia4 reductorfrecuencia4_1 (
    .Reloj(Reloj), .Activador(nivelvelocidad_1_velocidad1), .Reset(or_1_out),
    .RelojDividido(reductorfrecuencia4_1_relojdividido));
  ReductorFrecuencia2 reductorfrecuencia2_1 (
    .Reloj(Reloj), .Activador(nivelvelocidad_1_velocidad2), .Reset(or_2_out),
    .RelojDividido(reductorfrecuencia2_1_relojdividido));
  Button button_1 (.out(button_1_out));
  or or_3 (or_3_out, reductorfrecuencia4_1_relojdividido, reductorfrecuencia2_1_relojdividido, and_1_out);
  colisionesMemoria colisionesmemoria_1 (
    .colActual(movimientocuadrado_1_colactual), .filaActual(movimientocuadrado_1_filaactual));
  DotMatrix #(.matrixrows(1)) dotmatrix_1 (
    .col0(movimientocuadrado_1_inicio[4]), .col1(movimientocuadrado_1_inicio[3]),
    .col2(movimientocuadrado_1_inicio[2]), .col3(movimientocuadrado_1_inicio[1]),
    .col4(movimientocuadrado_1_inicio[0]));
  Button button_2 (.out(button_2_out));
  DotMatrix #(.matrixrows(8)) dotmatrix_2 (
    .col0(movimientocuadrado_1_col0), .col1(movimientocuadrado_1_col1), .col2(movimientocuadrado_1_col2),
    .col3(movimientocuadrado_1_col3), .col4(movimientocuadrado_1_col4));
  movimientoCuadrado movimientocuadrado_1 (
    .strart(button_1_out), .Clock(or_3_out), .izq(button_2_out), .der(button_4_out),
    .col0(movimientocuadrado_1_col0), .col1(movimientocuadrado_1_col1), .col2(movimientocuadrado_1_col2),
    .inicio(movimientocuadrado_1_inicio), .filaActual(movimientocuadrado_1_filaactual),
    .col3(movimientocuadrado_1_col3), .col4(movimientocuadrado_1_col4),
    .colActual(movimientocuadrado_1_colactual));
  Button button_3 (.out(button_3_out));
  Button button_4 (.out(button_4_out));
  Button button_5 (.out(button_5_out));
  Button button_6 (.out(button_6_out));
  Button button_7 (.out(button_7_out));
  Button button_8 (.out(button_8_out));
  guardarNuevoEstado guardarnuevoestado_1 (
    .Y_POS(movimientocuadrado_1_filaactual), .CLK(Reloj), .RESET(button_3_out), .WRITE_ENABLE(or_3_out),
    .COLLISION(button_5_out), .X_POS(movimientocuadrado_1_colactual), .COL_0(guardarnuevoestado_1_col_0),
    .COL_1(guardarnuevoestado_1_col_1), .COL_2(guardarnuevoestado_1_col_2),
    .COL_3(guardarnuevoestado_1_col_3), .COL_4(guardarnuevoestado_1_col_4));  // open: NEXT_BIT_TRIGGER, colisionDer, colisionIzq
  LED led_1 (.in(contadorbin_1_led1));
  contadorBin contadorbin_1 (
    .Entrada(button_6_out), .Suma5(button_7_out), .Reset(button_8_out), .Clock(Reloj),
    .Led1(contadorbin_1_led1), .Led2(contadorbin_1_led2), .Led3(contadorbin_1_led3),
    .Led4(contadorbin_1_led4), .Led5(contadorbin_1_led5), .Led6(contadorbin_1_led6),
    .Led7(contadorbin_1_led7), .Led8(contadorbin_1_led8), .Led9(contadorbin_1_led9),
    .Led10(contadorbin_1_led10));
  LED led_2 (.in(contadorbin_1_led2));
  LED led_3 (.in(contadorbin_1_led3));
  LED led_4 (.in(contadorbin_1_led4));
  LED led_5 (.in(contadorbin_1_led5));
  LED led_6 (.in(contadorbin_1_led6));
  LED led_7 (.in(contadorbin_1_led7));
  LED led_8 (.in(contadorbin_1_led8));
  LED led_9 (.in(contadorbin_1_led9));
  LED led_10 (.in(contadorbin_1_led10));
  Button button_9 (.out(button_9_out));
  Hex_Digit_Display hex_digit_display_1 (.value(contador2_1_puntos4));  // open: dp
  contador2 contador2_1 (
    .Reset(button_8_out), .Suma5(button_7_out), .Sumar1(button_6_out), .Clock(Reloj),
    .Puntos4(contador2_1_puntos4), .Puntos3(contador2_1_puntos3), .Puntos2(contador2_1_puntos2),
    .Puntos1(contador2_1_puntos1));
  Hex_Digit_Display hex_digit_display_2 (.value(contador2_1_puntos3));  // open: dp
  Hex_Digit_Display hex_digit_display_3 (.value(contador2_1_puntos2));  // open: dp
  Hex_Digit_Display hex_digit_display_4 (.value(contador2_1_puntos1));  // open: dp
  Comparator #(.mode("unsigned")) comparator_1 (
    .a(guardarnuevoestado_1_col_0), .b(8'h1), .gt(comparator_1_gt), .eq(comparator_1_eq));  // open: lt
  Comparator #(.mode("unsigned")) comparator_2 (
    .a(guardarnuevoestado_1_col_1), .b(8'h1), .gt(comparator_2_gt), .eq(comparator_2_eq));  // open: lt
  Comparator #(.mode("unsigned")) comparator_3 (
    .a(guardarnuevoestado_1_col_2), .b(8'h1), .gt(comparator_3_gt), .eq(comparator_3_eq));  // open: lt
  Comparator #(.mode("unsigned")) comparator_4 (
    .a(guardarnuevoestado_1_col_3), .b(8'h1), .gt(comparator_4_gt), .eq(comparator_4_eq));  // open: lt
  Comparator #(.mode("unsigned")) comparator_5 (
    .a(guardarnuevoestado_1_col_4), .b(8'h1), .gt(comparator_5_gt), .eq(comparator_5_eq));  // open: lt
  LED led_11 (.in(puntajerecord_1_led1));
  PuntajeRecord puntajerecord_1 (
    .LedEntrada1(contadorbin_1_led1), .LedEntrada2(contadorbin_1_led2), .LedEntrada3(contadorbin_1_led3),
    .LedEntrada4(contadorbin_1_led4), .LedEntrada5(contadorbin_1_led5), .LedEntrada6(contadorbin_1_led6),
    .LedEntrada7(contadorbin_1_led7), .LedEntrada8(contadorbin_1_led8), .LedEntrada9(contadorbin_1_led9),
    .LedEntrada10(contadorbin_1_led10), .ResetRecord(button_9_out), .Clock(Reloj),
    .Led1(puntajerecord_1_led1), .Led2(puntajerecord_1_led2), .Led3(puntajerecord_1_led3),
    .Led4(puntajerecord_1_led4), .Led5(puntajerecord_1_led5), .Led6(puntajerecord_1_led6),
    .Led7(puntajerecord_1_led7), .Led8(puntajerecord_1_led8), .Led9(puntajerecord_1_led9),
    .Led10(puntajerecord_1_led10));
  LED led_12 (.in(puntajerecord_1_led2));
  LED led_13 (.in(puntajerecord_1_led3));
  LED led_14 (.in(puntajerecord_1_led4));
  LED led_15 (.in(puntajerecord_1_led5));
  LED led_16 (.in(puntajerecord_1_led6));
  LED led_17 (.in(puntajerecord_1_led7));
  LED led_18 (.in(puntajerecord_1_led8));
  LED led_19 (.in(puntajerecord_1_led9));
  LED led_20 (.in(puntajerecord_1_led10));
  PuntajeRecordHexa puntajerecordhexa_1 (
    .Puntos4(contador2_1_puntos4), .Puntos3(contador2_1_puntos3), .Puntos2(contador2_1_puntos2),
    .Puntos1(contador2_1_puntos1), .Reset(button_9_out), .Clock(Reloj),
    .Record4(puntajerecordhexa_1_record4), .Record3(puntajerecordhexa_1_record3),
    .Record2(puntajerecordhexa_1_record2), .Record1(puntajerecordhexa_1_record1));
  or or_4 (or_4_out, comparator_1_gt, comparator_1_eq);
  or or_5 (or_5_out, comparator_2_gt, comparator_2_eq);
  or or_6 (or_6_out, comparator_3_gt, comparator_3_eq);
  or or_7 (or_7_out, comparator_4_gt, comparator_4_eq);
  or or_8 (or_8_out, comparator_5_gt, comparator_5_eq);
  Hex_Digit_Display hex_digit_display_5 (.value(puntajerecordhexa_1_record4));  // open: dp
  and and_2 (and_2_out, or_4_out, or_5_out, or_6_out, or_7_out, or_8_out);
  Hex_Digit_Display hex_digit_display_6 (.value(puntajerecordhexa_1_record3));  // open: dp
  Hex_Digit_Display hex_digit_display_7 (.value(puntajerecordhexa_1_record2));  // open: dp
  Hex_Digit_Display hex_digit_display_8 (.value(puntajerecordhexa_1_record1));  // open: dp
  assign bit_extender_1_out = {{2{1'b0}}, and_2_out};  // Bit_Extender bit_extender_1
  assign bit_extender_2_out = {{2{1'b0}}, and_2_out};  // Bit_Extender bit_extender_2
  assign bit_extender_3_out = {{2{1'b0}}, and_2_out};  // Bit_Extender bit_extender_3
  assign bit_extender_4_out = {{2{1'b0}}, and_2_out};  // Bit_Extender bit_extender_4
  assign bit_extender_5_out = {{2{1'b0}}, and_2_out};  // Bit_Extender bit_extender_5
  assign xor_1_out = movimientocuadrado_1_col0 ^ shifter_1_out;  // XOR_Gate xor_1, 8 bits wide
  assign xor_2_out = movimientocuadrado_1_col1 ^ shifter_2_out;  // XOR_Gate xor_2, 8 bits wide
  Shifter #(.shift("lr")) shifter_1 (.in(guardarnuevoestado_1_col_0), .\dist (bit_extender_1_out), .out(shifter_1_out));
  Shifter #(.shift("lr")) shifter_2 (.in(guardarnuevoestado_1_col_1), .\dist (bit_extender_2_out), .out(shifter_2_out));
  Shifter #(.shift("lr")) shifter_3 (.in(guardarnuevoestado_1_col_2), .\dist (bit_extender_3_out), .out(shifter_3_out));
  Shifter #(.shift("lr")) shifter_4 (.in(guardarnuevoestado_1_col_3), .\dist (bit_extender_4_out), .out(shifter_4_out));
  Shifter #(.shift("lr")) shifter_5 (.in(guardarnuevoestado_1_col_4), .\dist (bit_extender_5_out), .out(shifter_5_out));
  DotMatrix #(.matrixrows(8)) dotmatrix_3 (
    .col0(xor_1_out), .col1(xor_2_out), .col2(xor_3_out), .col3(xor_4_out), .col4(xor_5_out));
  assign xor_3_out = movimientocuadrado_1_col2 ^ shifter_3_out;  // XOR_Gate xor_3, 8 bits wide
  assign xor_4_out = movimientocuadrado_1_col3 ^ shifter_4_out;  // XOR_Gate xor_4, 8 bits wide
  assign xor_5_out = movimientocuadrado_1_col4 ^ shifter_5_out;  // XOR_Gate xor_5, 8 bits wide

  // Notes on the sheet:
  //   Configurar el reloj en 8hz para iniciar el juego
  //   - velocidad 1: menos de 10 bloques
  //   - velocidad 2: entre 10 y 20 bloques
  //   - velocidad 3: mas de 20 bloques
  //   Puntaje Actual
  //   Puntaje Record
endmodule

module contadorBin (
  input  Entrada,
  input  Suma5,
  input  Reset,
  input  Clock,
  output Led1,
  output Led2,
  output Led3,
  output Led4,
  output Led5,
  output Led6,
  output Led7,
  output Led8,
  output Led9,
  output Led10
);

  wire and_1_out, and_2_out, and_3_out, and_4_out, and_5_out, and_6_out, and_7_out, and_8_out, and_9_out,
       decoder_1_out1, decoder_1_out3, decoder_1_out5, decoder_1_out7, decoder_1_out9, decoder_1_out10,
       not_1_out, or_1_out, or_2_out, or_3_out;
  wire [3:0] counter_1_q;

  Counter #(.max('ha), .width(4)) counter_1 (
    .D(4'b1010), .Q(counter_1_q), .up(Entrada), .clk(or_1_out));  // open: load, count, carry, clr
  or or_1 (or_1_out, Suma5, and_1_out);
  and and_1 (and_1_out, Clock, not_1_out);
  Decoder #(.select(4)) decoder_1 (
    .out1(decoder_1_out1), .out3(decoder_1_out3), .out5(decoder_1_out5), .out7(decoder_1_out7),
    .out9(decoder_1_out9), .out10(decoder_1_out10), .sel(counter_1_q));  // open: out0, out2, out4, out6, out8, out11, out12, out13, out14, out15, en
  not not_1 (not_1_out, decoder_1_out10);
  or or_2 (or_2_out, decoder_1_out1, decoder_1_out3, decoder_1_out5, decoder_1_out7, decoder_1_out9);
  or or_3 (or_3_out, or_2_out, Entrada);
  J_K_Flip_Flop j_k_ff_1 (.J(or_3_out), .K(or_3_out), .clk(or_3_out), .Q(Led1), .reset(Reset));  // open: Qn, preset
  and and_2 (and_2_out, Led1, Led2);
  J_K_Flip_Flop j_k_ff_2 (.J(Led1), .K(Led1), .clk(or_3_out), .Q(Led2), .reset(Reset));  // open: Qn, preset
  and and_3 (and_3_out, and_2_out, Led3);
  J_K_Flip_Flop j_k_ff_3 (.J(and_2_out), .K(and_2_out), .clk(or_3_out), .Q(Led3), .reset(Reset));  // open: Qn, preset
  J_K_Flip_Flop j_k_ff_4 (.J(and_3_out), .K(and_3_out), .clk(or_3_out), .Q(Led4), .reset(Reset));  // open: Qn, preset
  and and_4 (and_4_out, and_3_out, Led4);
  J_K_Flip_Flop j_k_ff_5 (.J(and_4_out), .K(and_4_out), .clk(or_3_out), .Q(Led5), .reset(Reset));  // open: Qn, preset
  and and_5 (and_5_out, and_4_out, Led5);
  and and_6 (and_6_out, and_5_out, Led6);
  J_K_Flip_Flop j_k_ff_6 (.J(and_5_out), .K(and_5_out), .clk(or_3_out), .Q(Led6), .reset(Reset));  // open: Qn, preset
  J_K_Flip_Flop j_k_ff_7 (.J(and_6_out), .K(and_6_out), .clk(or_3_out), .Q(Led7), .reset(Reset));  // open: Qn, preset
  and and_7 (and_7_out, and_6_out, Led7);
  and and_8 (and_8_out, and_7_out, Led8);
  J_K_Flip_Flop j_k_ff_8 (.J(and_7_out), .K(and_7_out), .clk(or_3_out), .Q(Led8), .reset(Reset));  // open: Qn, preset
  J_K_Flip_Flop j_k_ff_9 (.J(and_8_out), .K(and_8_out), .clk(or_3_out), .Q(Led9), .reset(Reset));  // open: Qn, preset
  and and_9 (and_9_out, and_8_out, Led9);
  J_K_Flip_Flop j_k_ff_10 (.J(and_9_out), .K(and_9_out), .clk(or_3_out), .Q(Led10), .reset(Reset));  // open: Qn, preset
endmodule

module contador2 (
  input  Reset,
  input  Suma5,
  input  Sumar1,
  input  Clock,
  output [3:0] Puntos4,
  output [3:0] Puntos3,
  output [3:0] Puntos2,
  output [3:0] Puntos1
);

  wire and_1_out, counter_3_carry, counter_4_carry, counter_5_carry, decoder_1_out1, decoder_1_out3,
       decoder_1_out5, decoder_1_out7, decoder_1_out9, decoder_1_out10, not_1_out, not_2_out, not_3_out,
       not_4_out, or_1_out, or_2_out, or_3_out;
  wire [3:0] counter_1_q;

  Counter #(.max('ha), .width(4)) counter_1 (
    .D(4'b1010), .Q(counter_1_q), .up(Sumar1), .clk(or_1_out));  // open: load, count, carry, clr
  or or_1 (or_1_out, Suma5, and_1_out);
  and and_1 (and_1_out, Clock, not_1_out);
  Decoder #(.select(4)) decoder_1 (
    .out1(decoder_1_out1), .out3(decoder_1_out3), .out5(decoder_1_out5), .out7(decoder_1_out7),
    .out9(decoder_1_out9), .out10(decoder_1_out10), .sel(counter_1_q));  // open: out0, out2, out4, out6, out8, out11, out12, out13, out14, out15, en
  not not_1 (not_1_out, decoder_1_out10);
  or or_2 (or_2_out, decoder_1_out1, decoder_1_out3, decoder_1_out5, decoder_1_out7, decoder_1_out9);
  Counter #(.max('h9), .width(4)) counter_2 (
    .clr(Reset), .clk(not_2_out), .Q(Puntos4));  // open: load, up, count, D, carry
  Counter #(.max('h9), .width(4)) counter_3 (
    .clr(Reset), .clk(not_3_out), .carry(counter_3_carry), .Q(Puntos3));  // open: load, up, count, D
  Counter #(.max('h9), .width(4)) counter_4 (
    .clr(Reset), .clk(not_4_out), .carry(counter_4_carry), .Q(Puntos2));  // open: load, up, count, D
  Counter #(.max('h9), .width(4)) counter_5 (
    .clr(Reset), .clk(or_3_out), .carry(counter_5_carry), .Q(Puntos1));  // open: load, up, count, D
  or or_3 (or_3_out, or_2_out, Sumar1);
  not not_2 (not_2_out, counter_3_carry);
  not not_3 (not_3_out, counter_4_carry);
  not not_4 (not_4_out, counter_5_carry);
endmodule

module PuntajeRecord (
  input  LedEntrada1,
  input  LedEntrada2,
  input  LedEntrada3,
  input  LedEntrada4,
  input  LedEntrada5,
  input  LedEntrada6,
  input  LedEntrada7,
  input  LedEntrada8,
  input  LedEntrada9,
  input  LedEntrada10,
  input  ResetRecord,
  input  Clock,
  output Led1,
  output Led2,
  output Led3,
  output Led4,
  output Led5,
  output Led6,
  output Led7,
  output Led8,
  output Led9,
  output Led10
);

  wire and_1_out, comparator_1_gt;
  wire [9:0] d_ff_18_q;

  D_Flip_Flop d_ff_1 (.D(LedEntrada10), .clk(Clock), .Q(d_ff_18_q[9]));  // open: Qn, preset, reset
  D_Flip_Flop d_ff_2 (.D(LedEntrada9), .clk(Clock), .Q(d_ff_18_q[8]));  // open: Qn, preset, reset
  D_Flip_Flop d_ff_3 (.D(d_ff_18_q[9]), .clk(and_1_out), .Q(Led10), .reset(ResetRecord));  // open: Qn, preset
  D_Flip_Flop d_ff_4 (.D(LedEntrada8), .clk(Clock), .Q(d_ff_18_q[7]));  // open: Qn, preset, reset
  D_Flip_Flop d_ff_5 (.D(d_ff_18_q[8]), .clk(and_1_out), .Q(Led9), .reset(ResetRecord));  // open: Qn, preset
  D_Flip_Flop d_ff_6 (.D(LedEntrada7), .clk(Clock), .Q(d_ff_18_q[6]));  // open: Qn, preset, reset
  D_Flip_Flop d_ff_7 (.D(d_ff_18_q[7]), .clk(and_1_out), .Q(Led8), .reset(ResetRecord));  // open: Qn, preset
  D_Flip_Flop d_ff_8 (.D(LedEntrada6), .clk(Clock), .Q(d_ff_18_q[5]));  // open: Qn, preset, reset
  D_Flip_Flop d_ff_9 (.D(d_ff_18_q[6]), .clk(and_1_out), .Q(Led7), .reset(ResetRecord));  // open: Qn, preset
  D_Flip_Flop d_ff_10 (.D(LedEntrada5), .clk(Clock), .Q(d_ff_18_q[4]));  // open: Qn, preset, reset
  D_Flip_Flop d_ff_11 (.D(d_ff_18_q[5]), .clk(and_1_out), .Q(Led6), .reset(ResetRecord));  // open: Qn, preset
  D_Flip_Flop d_ff_12 (.D(LedEntrada4), .clk(Clock), .Q(d_ff_18_q[3]));  // open: Qn, preset, reset
  D_Flip_Flop d_ff_13 (.D(d_ff_18_q[4]), .clk(and_1_out), .Q(Led5), .reset(ResetRecord));  // open: Qn, preset
  D_Flip_Flop d_ff_14 (.D(LedEntrada3), .clk(Clock), .Q(d_ff_18_q[2]));  // open: Qn, preset, reset
  D_Flip_Flop d_ff_15 (.D(d_ff_18_q[3]), .clk(and_1_out), .Q(Led4), .reset(ResetRecord));  // open: Qn, preset
  Comparator #(.mode("unsigned"), .width(10)) comparator_1 (
    .a(d_ff_18_q), .b({Led10, Led9, Led8, Led7, Led6, Led5, Led4, Led3, Led2, Led1}), .gt(comparator_1_gt));  // open: eq, lt
  D_Flip_Flop d_ff_16 (.D(d_ff_18_q[2]), .clk(and_1_out), .Q(Led3), .reset(ResetRecord));  // open: Qn, preset
  D_Flip_Flop d_ff_17 (.D(LedEntrada2), .clk(Clock), .Q(d_ff_18_q[1]));  // open: Qn, preset, reset
  D_Flip_Flop d_ff_18 (.D(LedEntrada1), .clk(Clock), .Q(d_ff_18_q[0]));  // open: Qn, preset, reset
  D_Flip_Flop d_ff_19 (.D(d_ff_18_q[1]), .clk(and_1_out), .Q(Led2), .reset(ResetRecord));  // open: Qn, preset
  D_Flip_Flop d_ff_20 (.D(d_ff_18_q[0]), .clk(and_1_out), .Q(Led1), .reset(ResetRecord));  // open: Qn, preset
  and and_1 (and_1_out, comparator_1_gt, Clock);
endmodule

module PuntajeRecordHexa (
  input  [3:0] Puntos4,
  input  [3:0] Puntos3,
  input  [3:0] Puntos2,
  input  [3:0] Puntos1,
  input  Reset,
  input  Clock,
  output [3:0] Record4,
  output [3:0] Record3,
  output [3:0] Record2,
  output [3:0] Record1
);

  wire and_1_out, and_2_out, and_3_out, comparator_1_eq, comparator_1_gt, comparator_2_eq, comparator_2_gt,
       comparator_3_eq, comparator_3_gt, comparator_4_gt, or_1_out;

  Register #(.width(4)) register_1 (.D(Puntos4), .en(or_1_out), .clk(Clock), .Q(Record4), .clr(Reset));
  Register #(.width(4)) register_2 (.D(Puntos3), .en(or_1_out), .clk(Clock), .Q(Record3));  // open: clr
  Register #(.width(4)) register_3 (.D(Puntos2), .en(or_1_out), .clk(Clock), .Q(Record2), .clr(Reset));
  Register #(.width(4)) register_4 (.D(Puntos1), .en(or_1_out), .clk(Clock), .Q(Record1), .clr(Reset));
  Comparator #(.mode("unsigned"), .width(4)) comparator_1 (
    .a(Puntos4), .b(Record4), .gt(comparator_1_gt), .eq(comparator_1_eq));  // open: lt
  Comparator #(.mode("unsigned"), .width(4)) comparator_2 (
    .a(Puntos3), .b(Record3), .gt(comparator_2_gt), .eq(comparator_2_eq));  // open: lt
  Comparator #(.mode("unsigned"), .width(4)) comparator_3 (
    .a(Puntos2), .b(Record2), .gt(comparator_3_gt), .eq(comparator_3_eq));  // open: lt
  Comparator #(.mode("unsigned"), .width(4)) comparator_4 (
    .a(Puntos1), .b(Record1), .gt(comparator_4_gt));  // open: eq, lt
  and and_1 (and_1_out, comparator_1_eq, comparator_2_gt);
  and and_2 (and_2_out, comparator_1_eq, comparator_2_eq, comparator_3_gt);
  and and_3 (and_3_out, comparator_1_eq, comparator_2_eq, comparator_3_eq, comparator_4_gt);
  or or_1 (or_1_out, comparator_1_gt, and_1_out, and_2_out, and_3_out);
endmodule

module movimientoCuadrado (
  input  strart,
  input  Clock,
  input  izq,
  input  der,
  output [7:0] col0,
  output [7:0] col1,
  output [7:0] col2,
  output [4:0] inicio,
  output [7:0] filaActual,
  output [7:0] col3,
  output [7:0] col4,
  output [2:0] colActual
);

  wire and_2_out, and_3_out, and_4_out, and_5_out, and_6_out, and_7_out, button_1_out, button_2_out,
       button_3_out, comparator_1_eq, comparator_2_gt, d_ff_1_q, decoder_2_out0, decoder_2_out1,
       decoder_2_out2, decoder_2_out3, decoder_2_out4, not_1_out, not_2_out, not_3_out, not_4_out, not_5_out,
       not_6_out, not_7_out, not_8_out, or_1_out, or_2_out, or_3_out, or_4_out, or_5_out, or_6_out, or_7_out,
       random_1_p1, shift_register_2_out, shift_register_3_out, shift_register_4_out, shift_register_5_out,
       shift_register_6_out;
  wire [2:0] undriven;
  wire [7:0] shift_register_1_q7;

  Decoder #(.select(3)) decoder_1 (
    .out0(inicio[0]), .out1(inicio[3]), .out2(inicio[2]), .out3(inicio[1]), .out4(inicio[4]), .sel(undriven));  // open: out5, out6, out7, en
  DotMatrix #(.matrixrows(1)) dotmatrix_1 (
    .col0(inicio[0]), .col1(inicio[3]), .col2(inicio[2]), .col3(inicio[1]), .col4(inicio[4]));
  DotMatrix #(.matrixrows(8)) dotmatrix_2 (.col0(col0), .col1(col1), .col2(col2), .col3(col3), .col4(col4));
  Button button_1 (.out(button_1_out));
  or or_1 (or_1_out, not_1_out, comparator_1_eq);
  not not_1 (not_1_out, comparator_2_gt);
  or or_2 (or_2_out, button_2_out, izq);
  Button button_2 (.out(button_2_out));
  or or_3 (or_3_out, strart, button_1_out);
  // Random #(.width(3)) random_1: pin names not known; wires that end beside it: random_1_p1
  and and_1 (random_1_p1, or_1_out, not_3_out);
  and and_2 (and_2_out, comparator_2_gt, d_ff_1_q);
  Counter #(.max('h4), .ongoal("stay"), .width(3)) counter_1 (
    .load(and_2_out), .D(undriven), .count(or_4_out), .Q(colActual), .up(or_5_out), .clk(or_4_out));  // open: carry, clr
  or or_4 (or_4_out, or_2_out, and_2_out, or_5_out);
  Comparator #(.mode("unsigned")) comparator_1 (
    .a(shift_register_1_q7), .b(8'h40), .eq(comparator_1_eq));  // open: gt, lt
  Comparator #(.mode("unsigned"), .width(3)) comparator_2 (
    .a(3'b101), .b(undriven), .gt(comparator_2_gt));  // open: eq, lt
  Decoder #(.select(3)) decoder_2 (
    .out0(decoder_2_out0), .out1(decoder_2_out1), .out2(decoder_2_out2), .out3(decoder_2_out3),
    .out4(decoder_2_out4), .sel(colActual));  // open: out5, out6, out7, en
  or or_5 (or_5_out, der, button_3_out);
  not not_2 (not_2_out, d_ff_1_q);
  not not_3 (not_3_out, Clock);
  Button button_3 (.out(button_3_out));
  or or_6 (or_6_out, d_ff_1_q, or_3_out);
  Shift_Register shift_register_1 (
    .shift(not_2_out), .in(1'b0), .clk(Clock), .load(or_6_out), .d0(1'b1), .q0(shift_register_1_q7[7]),
    .d1(1'b0), .q1(shift_register_1_q7[6]), .d2(1'b0), .q2(shift_register_1_q7[5]), .d3(1'b0),
    .q3(shift_register_1_q7[4]), .d4(1'b0), .q4(shift_register_1_q7[3]), .d5(1'b0),
    .q5(shift_register_1_q7[2]), .d6(1'b0), .q6(shift_register_1_q7[1]), .d7(1'b0),
    .q7(shift_register_1_q7[0]));  // open: out, clr
  and and_3 (and_3_out, not_3_out, decoder_2_out0);
  and and_4 (and_4_out, not_3_out, decoder_2_out1);
  and and_5 (and_5_out, not_3_out, decoder_2_out2);
  and and_6 (and_6_out, not_3_out, decoder_2_out3);
  and and_7 (and_7_out, not_3_out, decoder_2_out4);
  not not_4 (not_4_out, decoder_2_out0);
  not not_5 (not_5_out, decoder_2_out1);
  not not_6 (not_6_out, decoder_2_out2);
  not not_7 (not_7_out, decoder_2_out3);
  not not_8 (not_8_out, decoder_2_out4);
  Shift_Register shift_register_2 (
    .clk(and_3_out), .out(shift_register_2_out), .load(and_3_out), .clr(not_4_out),
    .d0(shift_register_1_q7[7]), .q0(col0[7]), .d1(shift_register_1_q7[6]), .q1(col0[6]),
    .d2(shift_register_1_q7[5]), .q2(col0[5]), .d3(shift_register_1_q7[4]), .q3(col0[4]),
    .d4(shift_register_1_q7[3]), .q4(col0[3]), .d5(shift_register_1_q7[2]), .q5(col0[2]),
    .d6(shift_register_1_q7[1]), .q6(col0[1]), .d7(shift_register_1_q7[0]), .q7(col0[0]));  // open: shift, in
  Shift_Register shift_register_3 (
    .clk(and_4_out), .out(shift_register_3_out), .load(and_4_out), .clr(not_5_out),
    .d0(shift_register_1_q7[7]), .q0(col1[7]), .d1(shift_register_1_q7[6]), .q1(col1[6]),
    .d2(shift_register_1_q7[5]), .q2(col1[5]), .d3(shift_register_1_q7[4]), .q3(col1[4]),
    .d4(shift_register_1_q7[3]), .q4(col1[3]), .d5(shift_register_1_q7[2]), .q5(col1[2]),
    .d6(shift_register_1_q7[1]), .q6(col1[1]), .d7(shift_register_1_q7[0]), .q7(col1[0]));  // open: shift, in
  Shift_Register shift_register_4 (
    .clk(and_5_out), .out(shift_register_4_out), .load(and_5_out), .clr(not_6_out),
    .d0(shift_register_1_q7[7]), .q0(col2[7]), .d1(shift_register_1_q7[6]), .q1(col2[6]),
    .d2(shift_register_1_q7[5]), .q2(col2[5]), .d3(shift_register_1_q7[4]), .q3(col2[4]),
    .d4(shift_register_1_q7[3]), .q4(col2[3]), .d5(shift_register_1_q7[2]), .q5(col2[2]),
    .d6(shift_register_1_q7[1]), .q6(col2[1]), .d7(shift_register_1_q7[0]), .q7(col2[0]));  // open: shift, in
  Shift_Register shift_register_5 (
    .clk(and_6_out), .out(shift_register_5_out), .load(and_6_out), .clr(not_7_out),
    .d0(shift_register_1_q7[7]), .q0(col3[7]), .d1(shift_register_1_q7[6]), .q1(col3[6]),
    .d2(shift_register_1_q7[5]), .q2(col3[5]), .d3(shift_register_1_q7[4]), .q3(col3[4]),
    .d4(shift_register_1_q7[3]), .q4(col3[3]), .d5(shift_register_1_q7[2]), .q5(col3[2]),
    .d6(shift_register_1_q7[1]), .q6(col3[1]), .d7(shift_register_1_q7[0]), .q7(col3[0]));  // open: shift, in
  Shift_Register shift_register_6 (
    .clk(and_7_out), .out(shift_register_6_out), .load(and_7_out), .clr(not_8_out),
    .d0(shift_register_1_q7[7]), .q0(col4[7]), .d1(shift_register_1_q7[6]), .q1(col4[6]),
    .d2(shift_register_1_q7[5]), .q2(col4[5]), .d3(shift_register_1_q7[4]), .q3(col4[4]),
    .d4(shift_register_1_q7[3]), .q4(col4[3]), .d5(shift_register_1_q7[2]), .q5(col4[2]),
    .d6(shift_register_1_q7[1]), .q6(col4[1]), .d7(shift_register_1_q7[0]), .q7(col4[0]));  // open: shift, in
  or or_7 (or_7_out, shift_register_2_out, shift_register_3_out, shift_register_4_out, shift_register_5_out, shift_register_6_out);
  D_Flip_Flop d_ff_1 (.D(or_7_out), .clk(not_3_out), .Q(d_ff_1_q));  // open: Qn, preset, reset
  Multiplexer #(.select(3), .width(8)) multiplexer_1 (
    .in0(col0), .in1(col1), .in2(col2), .in3(col3), .in4(col4), .out(filaActual), .sel(colActual));  // open: in5, in6, in7
endmodule

module guardarNuevoEstado (
  input  [7:0] Y_POS,
  input  CLK,
  input  RESET,
  input  WRITE_ENABLE,
  input  COLLISION,
  input  [2:0] X_POS,
  output [7:0] COL_0,
  output [7:0] COL_1,
  output [7:0] COL_2,
  output [7:0] COL_3,
  output [7:0] COL_4,
  output NEXT_BIT_TRIGGER,
  output colisionDer,
  output colisionIzq
);

  wire and_2_out, and_3_out, and_4_out, and_5_out, and_6_out, and_7_out, and_8_out, and_9_out, and_10_out,
       and_11_out, and_12_out, and_13_out, and_14_out, CLK_t, clock_1_out, comparator_1_eq, comparator_1_lt,
       comparator_2_eq, comparator_2_lt, comparator_3_eq, comparator_3_lt, comparator_4_eq, comparator_4_lt,
       comparator_5_eq, comparator_5_lt, decoder_1_out0, decoder_1_out1, decoder_1_out2, decoder_1_out3,
       decoder_1_out4, or_2_out, or_3_out, or_4_out, or_5_out, or_6_out;
  wire [2:0] REG_X_q;
  wire [4:0] decoder_2_out0;
  wire [7:0] or_8_out, or_10_out, or_11_out, or_12_out, or_13_out, REG_Y_q;

  Clock clock_1 (.out(clock_1_out));
  or or_1 (CLK_t, clock_1_out, CLK);
  and and_1 (NEXT_BIT_TRIGGER, WRITE_ENABLE, COLLISION);
  Register REG_Y (.D(Y_POS), .en(NEXT_BIT_TRIGGER), .clk(CLK_t), .Q(REG_Y_q), .clr(RESET));
  Register #(.width(3)) REG_X (.D(X_POS), .en(NEXT_BIT_TRIGGER), .clk(CLK_t), .Q(REG_X_q), .clr(RESET));
  Comparator #(.mode("unsigned")) comparator_1 (
    .a(Y_POS), .b(COL_0), .eq(comparator_1_eq), .lt(comparator_1_lt));  // open: gt
  Comparator #(.mode("unsigned")) comparator_2 (
    .a(Y_POS), .b(COL_1), .eq(comparator_2_eq), .lt(comparator_2_lt));  // open: gt
  Comparator #(.mode("unsigned")) comparator_3 (
    .a(Y_POS), .b(COL_2), .eq(comparator_3_eq), .lt(comparator_3_lt));  // open: gt
  Comparator #(.mode("unsigned")) comparator_4 (
    .a(Y_POS), .b(COL_3), .eq(comparator_4_eq), .lt(comparator_4_lt));  // open: gt
  Comparator #(.mode("unsigned")) comparator_5 (
    .a(Y_POS), .b(COL_4), .eq(comparator_5_eq), .lt(comparator_5_lt));  // open: gt
  Comparator #(.mode("unsigned")) comparator_6 (.a(Y_POS), .b(8'h3));  // open: gt, eq, lt
  Decoder #(.select(3)) decoder_1 (
    .out0(decoder_1_out0), .out1(decoder_1_out1), .out2(decoder_1_out2), .out3(decoder_1_out3),
    .out4(decoder_1_out4), .sel(X_POS));  // open: out5, out6, out7, en
  Decoder #(.select(3)) decoder_2 (
    .out0(decoder_2_out0[0]), .out1(decoder_2_out0[1]), .out2(decoder_2_out0[2]), .out3(decoder_2_out0[3]),
    .out4(decoder_2_out0[4]), .sel(REG_X_q), .en(1'b1));  // open: out5, out6, out7
  or or_2 (or_2_out, comparator_1_eq, comparator_1_lt);
  or or_3 (or_3_out, comparator_2_eq, comparator_2_lt);
  or or_4 (or_4_out, comparator_3_eq, comparator_3_lt);
  or or_5 (or_5_out, comparator_4_eq, comparator_4_lt);
  or or_6 (or_6_out, comparator_5_eq, comparator_5_lt);
  and and_2 (and_2_out, decoder_1_out0, or_3_out);
  and and_3 (and_3_out, decoder_1_out1, or_4_out);
  and and_4 (and_4_out, decoder_1_out2, or_5_out);
  and and_5 (and_5_out, decoder_1_out3, or_6_out);
  or or_7 (colisionDer, and_2_out, and_3_out, and_4_out, and_5_out);
  assign or_8_out = COL_0 | REG_Y_q;  // OR_Gate or_8, 8 bits wide
  and and_6 (and_6_out, NEXT_BIT_TRIGGER, decoder_2_out0[0]);
  and and_7 (and_7_out, or_2_out, decoder_1_out1);
  and and_8 (and_8_out, or_3_out, decoder_1_out2);
  and and_9 (and_9_out, or_4_out, decoder_1_out3);
  and and_10 (and_10_out, or_5_out, decoder_1_out4);
  Register register_1 (.D(or_8_out), .en(and_6_out), .Q(COL_0), .clk(CLK_t), .clr(RESET));
  or or_9 (colisionIzq, and_7_out, and_8_out, and_9_out, and_10_out);
  assign or_10_out = COL_1 | REG_Y_q;  // OR_Gate or_10, 8 bits wide
  and and_11 (and_11_out, NEXT_BIT_TRIGGER, decoder_2_out0[1]);
  Register register_2 (.D(or_10_out), .en(and_11_out), .Q(COL_1), .clk(CLK_t), .clr(RESET));
  assign or_11_out = COL_2 | REG_Y_q;  // OR_Gate or_11, 8 bits wide
  and and_12 (and_12_out, NEXT_BIT_TRIGGER, decoder_2_out0[2]);
  Register register_3 (.D(or_11_out), .en(and_12_out), .Q(COL_2), .clk(CLK_t), .clr(RESET));
  assign or_12_out = COL_3 | REG_Y_q;  // OR_Gate or_12, 8 bits wide
  and and_13 (and_13_out, NEXT_BIT_TRIGGER, decoder_2_out0[3]);
  Register register_4 (.D(or_12_out), .en(and_13_out), .Q(COL_3), .clk(CLK_t), .clr(RESET));
  assign or_13_out = COL_4 | REG_Y_q;  // OR_Gate or_13, 8 bits wide
  and and_14 (and_14_out, NEXT_BIT_TRIGGER, decoder_2_out0[4]);
  Register register_5 (.D(or_13_out), .en(and_14_out), .Q(COL_4), .clk(CLK_t), .clr(RESET));
endmodule

module colisionesMemoria (
  input  [2:0] colActual,
  input  [7:0] filaActual
);

  wire clock_2_out, comparator_1_eq, comparator_2_eq;
  wire [7:0] ram_1_dout;

  Clock clock_1 ();  // open: out
  Comparator comparator_1 (.a(filaActual), .b(8'h1), .eq(comparator_1_eq));  // open: gt, lt
  Clock clock_2 (.out(clock_2_out));
  RAM #(.addrWidth(3)) ram_1 (
    .addr(colActual), .clk(clock_2_out), .din(filaActual), .dout(ram_1_dout));  // open: we, oe
  Comparator comparator_2 (.a(ram_1_dout), .b({8{1'b0}}), .eq(comparator_2_eq));  // open: gt, lt
endmodule

module ReductorFrecuencia2 (
  input  Reloj,
  input  Activador,
  input  Reset,
  output RelojDividido
);

  wire and_1_out, not_1_out;

  and and_1 (and_1_out, Reloj, Activador);
  Register #(.width(1)) register_1 (.D(not_1_out), .en(1'b1), .clk(and_1_out), .Q(RelojDividido), .clr(Reset));
  not not_1 (not_1_out, RelojDividido);
endmodule

module ReductorFrecuencia4 (
  input  Reloj,
  input  Activador,
  input  Reset,
  output RelojDividido
);

  wire and_1_out, not_1_out, not_2_out, register_1_q;

  and and_1 (and_1_out, Reloj, Activador);
  Register #(.width(1)) register_1 (.D(not_1_out), .en(1'b1), .clk(and_1_out), .Q(register_1_q), .clr(Reset));
  not not_1 (not_1_out, register_1_q);
  Register #(.width(1)) register_2 (.D(not_2_out), .en(1'b1), .clk(register_1_q), .Q(RelojDividido), .clr(Reset));
  not not_2 (not_2_out, RelojDividido);
endmodule

module ReductorFrecuencia8 (
  input  Reloj,
  input  Activador,
  input  Reset,
  output RelojDividido
);

  wire and_1_out, not_1_out, not_2_out, not_3_out, register_1_q, register_2_q;

  and and_1 (and_1_out, Reloj, Activador);
  Register #(.width(1)) register_1 (.D(not_1_out), .en(1'b1), .clk(and_1_out), .Q(register_1_q), .clr(Reset));
  not not_1 (not_1_out, register_1_q);
  Register #(.width(1)) register_2 (.D(not_2_out), .en(1'b1), .clk(register_1_q), .Q(register_2_q), .clr(Reset));
  not not_2 (not_2_out, register_2_q);
  Register #(.width(1)) register_3 (.D(not_3_out), .en(1'b1), .clk(register_2_q), .Q(RelojDividido), .clr(Reset));
  not not_3 (not_3_out, RelojDividido);
endmodule

module NivelVelocidad (
  input  Entrada,
  input  Reset,
  output velocidad1,
  output velocidad2,
  output velocidad3
);

  wire comparator_1_eq, comparator_1_gt, comparator_1_lt, comparator_2_eq, comparator_2_gt, comparator_2_lt,
       or_1_out;
  wire [4:0] counter_1_q;

  Counter #(.max('h1e), .ongoal("stay"), .width(5)) counter_1 (
    .Q(counter_1_q), .clk(Entrada), .clr(Reset));  // open: load, D, count, carry, up
  Comparator #(.mode("unsigned"), .width(5)) comparator_1 (
    .a(counter_1_q), .b(5'b01010), .gt(comparator_1_gt), .eq(comparator_1_eq), .lt(comparator_1_lt));
  Comparator #(.mode("unsigned"), .width(5)) comparator_2 (
    .a(counter_1_q), .b(5'b10100), .gt(comparator_2_gt), .eq(comparator_2_eq), .lt(comparator_2_lt));
  or or_1 (or_1_out, comparator_1_gt, comparator_1_eq);
  or or_2 (velocidad3, comparator_2_gt, comparator_2_eq);
  and and_1 (velocidad1, comparator_1_lt, comparator_2_lt);
  and and_2 (velocidad2, or_1_out, comparator_2_lt);
endmodule
